// Digital circuit lab2bitti.dig as structural Verilog
module lab2bitti (
  input  [3:0] in,
  output [7:0] out
);

  Add #(.Bits(6)) add_1 (.a({in, 2'b00}), .b({2'b00, in}), .c_i(1'b0), .s(out[5:0]));  // open: c_o

  assign out[7:6] = 2'b00;
endmodule
