// Digital circuit emrezeytinogluinlab3son.dig as structural Verilog
module emrezeytinogluinlab3son (
  input  MSB__A,
  input  B,
  input  LSB__C
);

  wire and_1_out, and_2_out, and_3_out, and_4_out, and_5_out, and_6_out, not_1_out, not_2_out, not_3_out,
       or_1_out, or_2_out;

  not not_1 (not_1_out, MSB__A);
  not not_2 (not_2_out, B);
  not not_3 (not_3_out, LSB__C);
  LED led_1 (.in(MSB__A));
  LED led_2 (.in(B));
  LED led_3 (.in(MSB__A));
  LED led_4 (.in(or_1_out));
  and and_1 (and_1_out, not_1_out, B);
  and and_2 (and_2_out, MSB__A, not_2_out);
  and and_3 (and_3_out, not_3_out, not_1_out, B);
  and and_4 (and_4_out, not_3_out, MSB__A, not_2_out);
  and and_5 (and_5_out, LSB__C, not_1_out, not_2_out);
  and and_6 (and_6_out, LSB__C, MSB__A, B);
  LED led_5 (.in(LSB__C));
  LED led_6 (.in(or_2_out));
  or or_1 (or_1_out, and_1_out, and_2_out);
  or or_2 (or_2_out, and_3_out, and_4_out, and_5_out, and_6_out);

  // Notes on the sheet:
  //   A
  //   B
  //   X
  //   Y
  //   C
  //   Z
  //   INPUT
  //   OUTPUT
endmodule
